# Fritzing sketch Project_Cyborg-Headpiece (saved by Fritzing 0.9.3b)

parts:
  Circuit_Playground = Adafruit Circuit Playground Dev Edition [part_number="Adafruit #3000"]
  NeoPixel_Ring = 24 NeoPixel Ring [part_number=1586]
  NeoPixel_Shield = Adafruit NeoPixel Shield [part_number="Adafruit #1430"]

nets:
  N1: Circuit_Playground.D6, NeoPixel_Shield.D6/DIN
  GND: Circuit_Playground.GND, NeoPixel_Ring.GND, NeoPixel_Shield.GND
  N2: Circuit_Playground.D3_SCL, NeoPixel_Ring.IN
  N3: Circuit_Playground.VBAT, NeoPixel_Ring.VDD, NeoPixel_Shield.PWRIN

custom parts:
  Adafruit Circuit Playground Dev Edition: Would you like to learn electronics, with an all-in-one board that has sensors and LEDs built in? Circuit Playground is here - and it's the best way to practice programming on real hardware with no soldering or sewing required! Circuit Playground features an ATmega32u4 processor, just like our popular Flora. The board's also round and has alligator-clip pads around it so you don't have to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
  24 NeoPixel Ring: 24 ultra bright smart LED NeoPixels are arranged in a circle with 2.6" (66mm) outer diameter. The rings are 'chainable' - connect the output pin of one to the input pin of another. Use only one microcontroller pin to control as many as you can chain together! Each LED is addressable as the driver chip is inside the LED. Each one has ~18mA constant current drive so the color will be very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
  Adafruit NeoPixel Shield: Put on your sunglasses before putting this shield onto your 'duino - 40 eye-blistering RGB LEDs adorn the NeoPixel shield for a blast of configurable color. Arranged in a 5x8 matrix, each pixel is individually addressable. Only one pin (Digital #6) is required to control all the LEDs. You can cut a trace and use nearly any other pin if you need some customization. To make it easy to start, the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
